// Digital circuit 3.1.dig as structural Verilog
module _3_1 (
  input  D,
  input  C,
  input  B,
  input  A,
  output Y
);

  wire not_1_out, not_2_out, not_3_out, not_4_out;

  not not_1 (not_1_out, A);
  not not_2 (not_2_out, A);
  not not_3 (not_3_out, A);
  not not_4 (not_4_out, A);
  Multiplexer #(.Selector_Bits(3)) multiplexer_1 (
    .sel({D, C, B}), .in_0(A), .in_1(A), .in_2(A), .in_3(A), .in_4(not_1_out), .in_5(not_2_out),
    .in_6(not_3_out), .in_7(not_4_out), .out(Y));

  // Notes on the sheet:
  //   Use A as the least-significant bit and 
  //   C as the most-significant bit.
  //   Converts between single bits & a 3-bit bus
endmodule
