// Digital circuit 3.2.dig as structural Verilog
module _3_2 (
  input  D,
  input  C,
  input  B,
  input  A,
  output Y
);

  wire not_1_out, not_2_out, not_3_out, not_4_out, not_5_out, not_6_out, not_7_out,
       one_cold_4_16_decoder_1_p2, one_cold_4_16_decoder_1_p3, one_cold_4_16_decoder_1_p4,
       one_cold_4_16_decoder_1_p5, one_cold_4_16_decoder_1_p6, one_cold_4_16_decoder_1_p7,
       one_cold_4_16_decoder_1_p8, or_1_out, or_2_out, or_3_out, or_4_out, or_5_out;

  // One_Cold_4_16_Decoder one_cold_4_16_decoder_1: pin names not known; wires that end beside it: {D, C, B, A}, one_cold_4_16_decoder_1_p2, one_cold_4_16_decoder_1_p3, one_cold_4_16_decoder_1_p4, one_cold_4_16_decoder_1_p5, one_cold_4_16_decoder_1_p6, one_cold_4_16_decoder_1_p7, one_cold_4_16_decoder_1_p8
  not not_1 (not_1_out, one_cold_4_16_decoder_1_p2);
  not not_2 (not_2_out, one_cold_4_16_decoder_1_p3);
  not not_3 (not_3_out, one_cold_4_16_decoder_1_p4);
  not not_4 (not_4_out, one_cold_4_16_decoder_1_p5);
  not not_5 (not_5_out, one_cold_4_16_decoder_1_p6);
  not not_6 (not_6_out, one_cold_4_16_decoder_1_p7);
  not not_7 (not_7_out, one_cold_4_16_decoder_1_p8);
  or or_1 (or_1_out, not_1_out, not_2_out);
  or or_2 (or_2_out, not_3_out, not_4_out);
  or or_3 (or_3_out, not_5_out, not_6_out);
  or or_4 (or_4_out, or_1_out, or_2_out);
  or or_5 (or_5_out, or_3_out, not_7_out);
  or or_6 (Y, or_4_out, or_5_out);

  // Notes on the sheet:
  //   D: MSB
  //   A: LSB
  //   Use D as the most-significant bit and 
  //   A as the least-significant bit.
  //   Converts between single bits & a 4-bit bus
endmodule
