// Digital circuit 3.3.dig as structural Verilog
module _3_3 (
  input  D,
  input  A,
  input  B,
  input  C,
  output Y
);

  wire and_1_out, and_2_out, not_1_out, not_2_out;

  not not_1 (not_1_out, D);
  not not_2 (not_2_out, A);
  and and_1 (and_1_out, 1'b1, not_1_out, A);
  and and_2 (and_2_out, 1'b1, not_2_out, D);
  or or_1 (Y, and_1_out, and_2_out);

  // Notes on the sheet:
  //   D: MSB
  //   A: LSB
  //   B: LSB
  //   C: LSB
  //   Use D as the most-significant bit and 
  //   A as the least-significant bit.
endmodule
