// Digital circuit 3.4.dig as structural Verilog
module _3_4 (
  input  D,
  input  C,
  input  B,
  input  A,
  output Y
);

  wire nand_1_out, nand_2_out, nand_3_out, nand_4_out, nand_5_out, nand_6_out, nand_7_out, nand_8_out;

  nand nand_1 (nand_1_out, A, A);
  nand nand_2 (nand_2_out, D, D);
  nand nand_3 (nand_3_out, D, nand_1_out);
  nand nand_4 (nand_4_out, nand_2_out, A);
  nand nand_5 (nand_5_out, nand_3_out, nand_3_out);
  nand nand_6 (nand_6_out, nand_4_out, nand_4_out);
  nand nand_7 (nand_7_out, nand_6_out, nand_6_out);
  nand nand_8 (nand_8_out, nand_5_out, nand_5_out);
  nand nand_9 (Y, nand_8_out, nand_7_out);

  // Notes on the sheet:
  //   D: MSB
  //   A: LSB
  //   Use D as the most-significant bit and 
  //   A as the least-significant bit.
endmodule
