// Digital circuit MUX design for lab 1.dig as structural Verilog
module MUX_design_for_lab_1 (
  input  C,
  input  B,
  input  A,
  input  D,
  output out_1
);

  wire _7404_1_pin2, _7404_1_pin9, _7404_1_pin11, _7404_1_pin13, notconnected_1_out, notconnected_2_out;

  // NotConnected on notconnected_1_out
  // NotConnected on notconnected_2_out
  _7404 _7404_1 (
    .pin1(D), .pin2(_7404_1_pin2), .pin3(notconnected_1_out), .pin5(notconnected_2_out), .pin7(1'b0),
    .pin9(_7404_1_pin9), .pin11(_7404_1_pin11), .pin13(_7404_1_pin13), .pin14(1'b1));  // open: pin4, pin6, pin8, pin10, pin12
  // NotConnected on _7404_1_pin13
  // NotConnected on _7404_1_pin11
  // NotConnected on _7404_1_pin9
  _74151 _74151_1 (
    .pin1(D), .pin2(D), .pin3(D), .pin4(D), .pin5(out_1), .pin7(1'b0), .pin8(1'b0), .pin9(A), .pin10(B),
    .pin11(C), .pin12(_7404_1_pin2), .pin13(_7404_1_pin2), .pin14(_7404_1_pin2), .pin15(_7404_1_pin2),
    .pin16(1'b1));  // open: pin6
endmodule
